// Digital circuit Flugzeug-Warnlampe.dig as structural Verilog
module Flugzeug_Warnlampe (
  input  Sensor1,
  input  Sensor2,
  input  Sensor3,
  output Warnlampe
);

  wire and_1_out, and_2_out, and_3_out;

  and and_1 (and_1_out, Sensor3, Sensor1);
  and and_2 (and_2_out, Sensor1, Sensor2);
  and and_3 (and_3_out, Sensor2, Sensor3);
  or or_1 (Warnlampe, and_1_out, and_2_out, and_3_out);
endmodule
